// Logisim project all_flipflop.circ as structural Verilog: 1 circuit, main circuit main
module main (
  input  in_1,
  input  in_2,
  input  in_3,
  input  in_4
);

  wire and_1_out, and_2_out, and_3_out, and_4_out, clock_1_out, clock_2_out, nor_1_out, nor_2_out, nor_3_out,
       nor_4_out;

  Clock clock_1 (.out(clock_1_out));
  Clock clock_2 (.out(clock_2_out));
  and and_1 (and_1_out, in_1, clock_1_out);
  and and_2 (and_2_out, clock_1_out, in_2);
  and and_3 (and_3_out, nor_3_out, in_3, clock_2_out);
  and and_4 (and_4_out, clock_2_out, in_4, nor_4_out);
  nor nor_1 (nor_1_out, and_1_out, nor_2_out);
  nor nor_2 (nor_2_out, nor_1_out, and_2_out);
  nor nor_3 (nor_3_out, and_3_out, nor_3_out);
  nor nor_4 (nor_4_out, nor_4_out, and_4_out);
  LED led_1 (.in(nor_1_out));
  LED led_2 (.in(nor_2_out));
  LED led_3 (.in(nor_3_out));
  LED led_4 (.in(nor_4_out));
endmodule
