// Logisim project fulladdersubtractor.circ as structural Verilog: 1 circuit, main circuit main
module main (
  input  _4,
  input  _2,
  input  _1,
  input  A,
  input  in_5,
  input  in_6,
  input  in_7,
  input  in_8,
  input  B
);

  wire n7486_1_pin3, n7486_1_pin6, n7486_1_pin7, n7486_1_pin8, n7486_1_pin11, n7486_1_pin14, n74283_1_pin1,
       n74283_1_pin4, n74283_1_pin9, n74283_1_pin10, n74283_1_pin13;

  _7486 #(.VccGndPorts("true")) u_7486_1 (
    .pin1(in_5), .pin2(_2), .pin3(n7486_1_pin3), .pin4(in_5), .pin5(_4), .pin6(n7486_1_pin6),
    .pin7(n7486_1_pin7), .pin14(n7486_1_pin14), .pin13(in_5), .pin12(A), .pin11(n7486_1_pin11), .pin10(in_5),
    .pin9(_1), .pin8(n7486_1_pin8));
  _74283 #(.VccGndPorts("true")) u_74283_1 (
    .pin1(n74283_1_pin1), .pin2(in_8), .pin3(n7486_1_pin8), .pin4(n74283_1_pin4), .pin5(n7486_1_pin11),
    .pin6(B), .pin7(in_5), .pin8(n7486_1_pin7), .pin16(n7486_1_pin14), .pin15(in_7), .pin14(n7486_1_pin3),
    .pin13(n74283_1_pin13), .pin12(n7486_1_pin6), .pin11(in_6), .pin10(n74283_1_pin10), .pin9(n74283_1_pin9));
  LED led_1 (.in(n74283_1_pin10));
  LED led_2 (.in(n74283_1_pin9));
  LED led_3 (.in(n74283_1_pin13));
  LED led_4 (.in(n74283_1_pin1));
  LED led_5 (.in(n74283_1_pin4));
  // also tied to GND on the sheet: n7486_1_pin7
  // also tied to VCC on the sheet: n7486_1_pin14

  // Notes on the sheet:
  //   Control
  //   Switch
  //   0
endmodule
